# Fritzing sketch CLDC001 (saved by Fritzing 0.9.1b)
circuit board: 4.8934cm x 3.20467cm
breadboards: 1

parts:
  CLDC001-PIC = CLSC001-PIC [package=THT]
  220ohm = Resistor [tolerance=±5% resistance=220 package=THT]
  Pot = Trimmer Potentiometer [maximum_resistance=10kΩ package=THT]
  U3 = AVR_MINI_PROG [package=avr_mini_prog]
  LCD1 = LCD screen
  J1 = longpad pin header, 4 pins [form="long pad"]  # not connected

nets:
  VCC: CLDC001-PIC.+V, 220ohm.Pin_1, U3.VCC, LCD1.VDD
  N1: CLDC001-PIC.Sensor_4_(RC3), LCD1.DB7
  N2: CLDC001-PIC.TX, U3.MISO
  N3: CLDC001-PIC.RX, U3.RST
  N4: CLDC001-PIC.Sensor_3_(RC2), LCD1.DB6
  N5: CLDC001-PIC.Sensor_2_(RC1), LCD1.DB5
  N6: CLDC001-PIC.Sensor_1_(RC0), LCD1.DB4
  N7: CLDC001-PIC.17, LCD1.RS
  N8: CLDC001-PIC.18, LCD1.E
  N9: CLDC001-PIC.0V, Pot.wiper, U3.SCK, LCD1.VSS, LCD1.R/W, LCD1.LED-
  N10: 220ohm.Pin_0, LCD1.LED+
  N11: Pot.leg2, LCD1.V0

notes:
  CLDC001
