# Fritzing sketch CLSC001_2 (saved by Fritzing 0.9.1b)
circuit board: 4.08578cm x 5.21498cm
breadboards: 1

parts:
  CLSC001-PIC = CLSC001-PIC [package=THT]
  X1 = USB Connectors [package=usb-a-s-nosilk-female]
  S1 = AUDIO-JACK2 [package=audio-jack]
  S2 = AUDIO-JACK2 [package=audio-jack]
  S3 = AUDIO-JACK2 [package=audio-jack]
  S4 = AUDIO-JACK2 [package=audio-jack]
  4_7k = Resistor [tolerance=±5% resistance=4.7k package=THT]
  4_7k_2 = Resistor [tolerance=±5% resistance=4.7k package=THT]
  4_7k_3 = Resistor [tolerance=±5% resistance=4.7k package=THT]
  4_7k_4 = Resistor [tolerance=±5% resistance=4.7k package=THT]

nets:
  N1: CLSC001-PIC.+V, X1.VBUS, S1.TIP, S2.TIP, S3.TIP, S4.TIP, 4_7k.Pin_1, 4_7k_2.Pin_1, 4_7k_3.Pin_1, 4_7k_4.Pin_1
  N2: CLSC001-PIC.Sensor_4_(RC3), S4.RING, 4_7k.Pin_0
  N3: CLSC001-PIC.TX, X1.D-
  N4: CLSC001-PIC.RX, X1.D+
  N5: CLSC001-PIC.Sensor_3_(RC2), S3.RING, 4_7k_4.Pin_0
  N6: CLSC001-PIC.Sensor_2_(RC1), S2.RING, 4_7k_3.Pin_0
  N7: CLSC001-PIC.Sensor_1_(RC0), S1.RING, 4_7k_2.Pin_0
  N8: CLSC001-PIC.0V, X1.GND, S1.SLEEVE, S2.SLEEVE, S3.SLEEVE, S4.SLEEVE

notes:
  CLSC001
