# Fritzing sketch MainBoard (saved by Fritzing 0.9.1b)
circuit board: 4.16322cm x 7.14845cm
breadboards: 1

parts:
  IC1 = IC, DIP package, 20 pins [chip_label=CLCP001]
  Power_plug1 = Power plug
  X1 = USB Connectors [package=usb-a-s]
  X2 = USB Connectors [package=usb-a-s]
  X3 = USB Connectors [package=usb-a-s]
  X4 = USB Connectors [package=usb-a-s]
  J1 = female pin header, 4 pins [form="♀ (female)"]
  R1 = Resistor [tolerance=±5% resistance=220 package=THT]

nets:
  N1: IC1.pin1, Power_plug1.VCC, X1.VBUS, X2.VBUS, X3.VBUS, X4.VBUS, J1.pin4, R1.Pin_0
  N2: IC1.pin10, X1.D-, X2.D-, X3.D-, X4.D-, J1.pin1, R1.Pin_1
  GND: IC1.pin20, Power_plug1.GND, X1.GND, X2.GND, X3.GND, X4.GND, J1.pin2
